// Digital circuit ALU.dig as structural Verilog
module ALU (
  input  [15:0] Left_Hand_Bus,
  input  [15:0] Right_Hand_Bus,
  input  Carry_In,
  input  And,
  input  Or,
  input  Xor,
  input  Subract_Mode,
  input  Sum_Out,
  input  Left,
  input  Shift,
  input  Rotate,
  input  Use_Carry,
  output [15:0] Result,
  output Carry_Out,
  output Signed,
  output Overflow,
  output Zero
);

  wire _74283_1_pin9, _74283_2_pin9, _74283_3_pin9, _74283_4_pin9, and_1_out, and_2_out, and_4_out,
       and_5_out, and_6_out, and_7_out, and_8_out, and_9_out, and_10_out, and_11_out, not_1_out, not_2_out,
       or_4_out, xor_2_out, xor_4_out, xor_5_out;
  wire [0:0] or_2_out;
  wire [15:0] _74283_2_pin4, and_3_out, or_1_out, xor_1_out, xor_3_out;
  wire [15:15] or_3_out;

  not not_1 (not_1_out, Rotate);
  and and_1 (and_1_out, Carry_In, Use_Carry);
  and and_2 (and_2_out, not_1_out, and_1_out);
  assign and_3_out = Left_Hand_Bus & Right_Hand_Bus;  // And and_3, 16 bits wide
  assign or_1_out = Left_Hand_Bus | Right_Hand_Bus;  // Or or_1, 16 bits wide
  assign xor_1_out = Left_Hand_Bus ^ Right_Hand_Bus;  // XOr xor_1, 16 bits wide
  and and_4 (and_4_out, Right_Hand_Bus[15], Rotate);
  and and_5 (and_5_out, Left, Shift);
  and and_6 (and_6_out, Right_Hand_Bus[0], Rotate);
  assign Result = And ? and_3_out : 16'bz;  // Driver driver_1
  assign Result = Or ? or_1_out : 16'bz;  // Driver driver_2
  assign Result = Xor ? xor_1_out : 16'bz;  // Driver driver_3
  or or_2 (or_2_out[0], and_4_out, and_2_out);
  and and_7 (and_7_out, Right_Hand_Bus[15], and_5_out);
  and and_8 (and_8_out, not_2_out, Shift);
  not not_2 (not_2_out, Left);
  and and_9 (and_9_out, and_8_out, Right_Hand_Bus[0]);
  or or_3 (or_3_out[15], and_6_out, and_2_out);
  or or_4 (or_4_out, and_7_out, and_9_out);
  assign Result = and_5_out ? {Right_Hand_Bus[14:0], or_2_out[0]} : 16'bz;  // Driver driver_4
  and and_10 (and_10_out, or_4_out, not_1_out);
  assign Result = and_8_out ? {or_3_out[15], Right_Hand_Bus[15:1]} : 16'bz;  // Driver driver_5
  xor xor_2 (xor_2_out, Carry_In, Subract_Mode);
  assign xor_3_out = Right_Hand_Bus ^ {16{Subract_Mode}};  // XOr xor_3, 16 bits wide
  _74283 _74283_1 (
    .pin1(_74283_2_pin4[1]), .pin2(xor_3_out[1]), .pin3(Left_Hand_Bus[1]), .pin4(_74283_2_pin4[0]),
    .pin5(Left_Hand_Bus[0]), .pin6(xor_3_out[0]), .pin7(xor_2_out), .pin8(1'b0), .pin9(_74283_1_pin9),
    .pin10(_74283_2_pin4[3]), .pin11(xor_3_out[3]), .pin12(Left_Hand_Bus[3]), .pin13(_74283_2_pin4[2]),
    .pin14(Left_Hand_Bus[2]), .pin15(xor_3_out[2]), .pin16(1'b1));
  _74283 _74283_2 (
    .pin1(_74283_2_pin4[5]), .pin2(xor_3_out[5]), .pin3(Left_Hand_Bus[5]), .pin4(_74283_2_pin4[4]),
    .pin5(Left_Hand_Bus[4]), .pin6(xor_3_out[4]), .pin7(_74283_1_pin9), .pin8(1'b0), .pin9(_74283_2_pin9),
    .pin10(_74283_2_pin4[7]), .pin11(xor_3_out[7]), .pin12(Left_Hand_Bus[7]), .pin13(_74283_2_pin4[6]),
    .pin14(Left_Hand_Bus[6]), .pin15(xor_3_out[6]), .pin16(1'b1));
  _74283 _74283_3 (
    .pin1(_74283_2_pin4[9]), .pin2(xor_3_out[9]), .pin3(Left_Hand_Bus[9]), .pin4(_74283_2_pin4[8]),
    .pin5(Left_Hand_Bus[8]), .pin6(xor_3_out[8]), .pin7(_74283_2_pin9), .pin8(1'b0), .pin9(_74283_3_pin9),
    .pin10(_74283_2_pin4[11]), .pin11(xor_3_out[11]), .pin12(Left_Hand_Bus[11]), .pin13(_74283_2_pin4[10]),
    .pin14(Left_Hand_Bus[10]), .pin15(xor_3_out[10]), .pin16(1'b1));
  _74283 _74283_4 (
    .pin1(_74283_2_pin4[13]), .pin2(xor_3_out[13]), .pin3(Left_Hand_Bus[13]), .pin4(_74283_2_pin4[12]),
    .pin5(Left_Hand_Bus[12]), .pin6(xor_3_out[12]), .pin7(_74283_3_pin9), .pin8(1'b0), .pin9(_74283_4_pin9),
    .pin10(_74283_2_pin4[15]), .pin11(xor_3_out[15]), .pin12(Left_Hand_Bus[15]), .pin13(_74283_2_pin4[14]),
    .pin14(Left_Hand_Bus[14]), .pin15(xor_3_out[14]), .pin16(1'b1));
  and and_11 (and_11_out, _74283_4_pin9, Sum_Out);
  or or_5 (Carry_Out, and_11_out, and_10_out);
  assign Result = Sum_Out ? _74283_2_pin4 : 16'bz;  // Driver driver_6
  nor nor_1 (Zero, Result[7], Result[6], Result[5], Result[4], Result[3], Result[2], Result[1], Result[0], Result[8], Result[9], Result[10], Result[11], Result[12], Result[13], Result[14], Result[15]);
  xor xor_4 (xor_4_out, Left_Hand_Bus[15], Result[15]);
  xor xor_5 (xor_5_out, Result[15], Right_Hand_Bus[15]);
  and and_12 (Overflow, xor_4_out, xor_5_out);

  assign Signed = Result[15];

  // Other names for the same wires on the sheet: CarryIn = Carry_In; LHSign = Left_Hand_Bus[15];
  //   RHSign = Right_Hand_Bus[15]

  // Notes on the sheet:
  //   Left_Hand_Bus: Left hand input of operation.
  //   Ignored for logical shift operations
  //   Right_Hand_Bus: Right hand input of operations.
  //   Used for logical shift operations
  //   Result: Result of the operation
  //   Carry_Out: Carry flag from the most recent operation.
  //   Carry flag is set from the following operations:
  //   Add
  //   Subract
  //   Shift
  //   Signed: Flag if the result is signed. Set by all operations
  //   (Might want to take off the and/or/etc from setting this
  //   Zero: Zero flag. Set by all operations if the result is Zero
  //   Left: Else right
  //   Shift: Activate shift or rotate if rotate is also set
  //   Get sign bit of inputs
endmodule
